// Logisim project maintained-mutually-exclusive-switch-bank_HtoL.circ as structural Verilog: 1 circuit, main circuit main
module main (
);

  wire button_1_out, button_2_out, button_3_out, button_4_out, d_ff_1_qn, d_ff_2_qn, d_ff_3_qn, d_ff_4_qn,
       nand_1_out, not_1_out, not_2_out, not_3_out, not_4_out;

  Button button_1 (.out(button_1_out));
  Button button_2 (.out(button_2_out));
  Button button_3 (.out(button_3_out));
  Button button_4 (.out(button_4_out));
  not not_1 (not_1_out, button_1_out);
  not not_2 (not_2_out, button_2_out);
  not not_3 (not_3_out, button_3_out);
  not not_4 (not_4_out, button_4_out);
  nand nand_1 (nand_1_out, not_1_out, not_2_out, not_3_out, not_4_out);
  D_Flip_Flop d_ff_1 (.clk(nand_1_out), .D(not_1_out), .Qn(d_ff_1_qn));  // open: Q, preset, en, reset
  LED led_1 (.in(d_ff_1_qn));
  D_Flip_Flop d_ff_2 (.clk(nand_1_out), .D(not_2_out), .Qn(d_ff_2_qn));  // open: Q, preset, en, reset
  LED led_2 (.in(d_ff_2_qn));
  D_Flip_Flop d_ff_3 (.clk(nand_1_out), .D(not_3_out), .Qn(d_ff_3_qn));  // open: Q, preset, en, reset
  LED led_3 (.in(d_ff_3_qn));
  D_Flip_Flop d_ff_4 (.clk(nand_1_out), .D(not_4_out), .Qn(d_ff_4_qn));  // open: Q, preset, en, reset
  LED led_4 (.in(d_ff_4_qn));

  // Notes on the sheet:
  //   maintained mutually-exclusive switch-bank
endmodule
