// Logisim project alternate-mutually-exclusive-switch-bank_HtoL.circ as structural Verilog: 1 circuit, main circuit main
module main (
);

  wire button_1_out, button_2_out, button_3_out, button_4_out, j_k_ff_1_q, j_k_ff_2_q, j_k_ff_3_q,
       j_k_ff_4_q, nand_1_out, not_1_out, not_2_out, not_3_out, not_4_out, not_5_out, not_6_out, not_7_out,
       not_8_out;

  Button button_1 (.out(button_1_out));
  not not_1 (not_1_out, button_1_out);
  not not_2 (not_2_out, button_2_out);
  Button button_2 (.out(button_2_out));
  Button button_3 (.out(button_3_out));
  not not_3 (not_3_out, button_3_out);
  Button button_4 (.out(button_4_out));
  not not_4 (not_4_out, button_4_out);
  nand nand_1 (nand_1_out, not_1_out, not_2_out, not_3_out, not_4_out);
  not not_5 (not_5_out, not_1_out);
  not not_6 (not_6_out, not_2_out);
  not not_7 (not_7_out, not_3_out);
  not not_8 (not_8_out, not_4_out);
  J_K_Flip_Flop j_k_ff_1 (
    .J(not_5_out), .clk(nand_1_out), .K(nand_1_out), .Q(j_k_ff_1_q));  // open: Qn, preset, en, reset
  J_K_Flip_Flop j_k_ff_2 (
    .J(not_6_out), .clk(nand_1_out), .K(nand_1_out), .Q(j_k_ff_2_q));  // open: Qn, preset, en, reset
  J_K_Flip_Flop j_k_ff_3 (
    .J(not_7_out), .clk(nand_1_out), .K(nand_1_out), .Q(j_k_ff_3_q));  // open: Qn, preset, en, reset
  J_K_Flip_Flop j_k_ff_4 (
    .J(not_8_out), .clk(nand_1_out), .K(nand_1_out), .Q(j_k_ff_4_q));  // open: Qn, preset, en, reset
  LED led_1 (.in(j_k_ff_1_q));
  LED led_2 (.in(j_k_ff_2_q));
  LED led_3 (.in(j_k_ff_3_q));
  LED led_4 (.in(j_k_ff_4_q));

  // Notes on the sheet:
  //   alternate mutually-exclusive switch-bank
endmodule
