// Logisim project momentary-mutually-inclusive-switch-bank_HtoL.circ as structural Verilog: 1 circuit, main circuit main
module main (
);

  wire button_1_out, button_2_out, button_3_out, button_4_out, not_1_out, not_2_out, not_3_out, not_4_out,
       not_5_out, not_6_out, not_7_out, not_8_out;

  Button button_1 (.out(button_1_out));
  Button button_2 (.out(button_2_out));
  Button button_3 (.out(button_3_out));
  Button button_4 (.out(button_4_out));
  not not_1 (not_1_out, button_1_out);
  not not_2 (not_2_out, button_2_out);
  not not_3 (not_3_out, button_3_out);
  not not_4 (not_4_out, button_4_out);
  not not_5 (not_5_out, not_1_out);
  not not_6 (not_6_out, not_2_out);
  not not_7 (not_7_out, not_3_out);
  not not_8 (not_8_out, not_4_out);
  LED led_1 (.in(not_5_out));
  LED led_2 (.in(not_6_out));
  LED led_3 (.in(not_7_out));
  LED led_4 (.in(not_8_out));

  // Notes on the sheet:
  //   momentary mutually-inclusive switch-bank
endmodule
